// Digital circuit 4-bit Register.dig as structural Verilog
module _4_bit_Register (
  input  LD,
  input  CLK,
  input  [3:0] D,
  input  ST,
  input  CLR,
  output [3:0] out
);

  wire and_1_out, and_2_out, and_3_out, and_4_out, and_5_out;

  and and_1 (and_1_out, CLK, ST);
  and and_2 (and_2_out, D[0], LD);
  and and_3 (and_3_out, D[1], LD);
  and and_4 (and_4_out, D[2], LD);
  and and_5 (and_5_out, D[3], LD);
  D_FF_AS D0 (.Set(1'b0), .D(and_2_out), .C(and_1_out), .Clr(CLR), .Q(out[0]));  // open: nQ
  D_FF_AS D1 (.Set(1'b0), .D(and_3_out), .C(and_1_out), .Clr(CLR), .Q(out[1]));  // open: nQ
  D_FF_AS D2 (.Set(1'b0), .D(and_4_out), .C(and_1_out), .Clr(CLR), .Q(out[2]));  // open: nQ
  D_FF_AS D3 (.Set(1'b0), .D(and_5_out), .C(and_1_out), .Clr(CLR), .Q(out[3]));  // open: nQ
endmodule
