// Digital circuit GPR.dig as structural Verilog
module GPR (
  input  [1:0] CTRL,
  input  [3:0] Input,
  input  clk,
  input  [1:0] Address,
  output [3:0] Output
);

  wire and_1_out, and_2_out, and_3_out, and_4_out, decoder_1_out_0, decoder_1_out_1, decoder_1_out_2,
       decoder_1_out_3;
  wire [3:0] _4_bit_register_1_output, _4_bit_register_2_output, _4_bit_register_3_output,
       _4_bit_register_4_output;

  Decoder #(.Selector_Bits(2)) decoder_1 (
    .sel(Address), .out_0(decoder_1_out_0), .out_1(decoder_1_out_1), .out_2(decoder_1_out_2),
    .out_3(decoder_1_out_3));
  and and_1 (and_1_out, clk, decoder_1_out_0);
  and and_2 (and_2_out, clk, decoder_1_out_1);
  and and_3 (and_3_out, clk, decoder_1_out_2);
  and and_4 (and_4_out, clk, decoder_1_out_3);
  _4_bit_Register _4_bit_register_1 (.CTRL(CTRL), .Input(Input), .clk(and_1_out), .Output(_4_bit_register_1_output));
  _4_bit_Register _4_bit_register_2 (.CTRL(CTRL), .Input(Input), .clk(and_2_out), .Output(_4_bit_register_2_output));
  _4_bit_Register _4_bit_register_3 (.CTRL(CTRL), .Input(Input), .clk(and_3_out), .Output(_4_bit_register_3_output));
  _4_bit_Register _4_bit_register_4 (.CTRL(CTRL), .Input(Input), .clk(and_4_out), .Output(_4_bit_register_4_output));
  Multiplexer #(.Selector_Bits(2), .Bits(4)) multiplexer_1 (
    .sel(Address), .in_0(_4_bit_register_1_output), .in_1(_4_bit_register_2_output),
    .in_2(_4_bit_register_3_output), .in_3(_4_bit_register_4_output), .out(Output));
endmodule
