// Digital circuit IR.dig as structural Verilog
module IR (
  input  CLK,
  input  RST,
  input  [3:0] Manual,
  input  [3:0] DRAM_output,
  input  LD,
  input  sel,
  output [3:0] IR_out
);

  wire [3:0] multiplexer_1_out, multiplexer_2_out;

  Multiplexer #(.Bits(4)) multiplexer_1 (.sel(sel), .in_0(DRAM_output), .in_1(Manual), .out(multiplexer_1_out));
  Multiplexer #(.Bits(4)) multiplexer_2 (.sel(LD), .in_0(IR_out), .in_1(multiplexer_1_out), .out(multiplexer_2_out));
  _4_bit_Register IR_Register (.LD(1'b1), .CLK(CLK), .D(multiplexer_2_out), .ST(1'b1), .CLR(RST), .out(IR_out));
endmodule
