// Digital circuit PC.dig as structural Verilog
module PC (
  input  INC,
  input  [3:0] Manual_Address,
  input  CLK,
  input  RST,
  input  LD,
  output [3:0] PC_plus_1
);

  wire [3:0] _4_bit_register_1_out, multiplexer_1_out, multiplexer_2_out;

  _4_bit_Register _4_bit_register_1 (
    .LD(1'b1), .CLK(CLK), .D(multiplexer_2_out), .ST(1'b1), .CLR(RST), .out(_4_bit_register_1_out));
  Multiplexer #(.Bits(4)) multiplexer_1 (.sel(INC), .in_0(4'b0000), .in_1(4'b0001), .out(multiplexer_1_out));
  Add #(.Bits(4)) add_1 (.a(_4_bit_register_1_out), .b(multiplexer_1_out), .c_i(1'b0), .s(PC_plus_1));  // open: c_o
  Multiplexer #(.Bits(4)) multiplexer_2 (.sel(LD), .in_0(PC_plus_1), .in_1(Manual_Address), .out(multiplexer_2_out));
endmodule
