// Digital circuit Registers DRAM.dig as structural Verilog
module Registers_DRAM (
  input  nOE,
  input  nRW,
  input  nCS,
  input  [3:0] Data,
  input  CLK,
  input  SEL,
  input  IR_LD,
  input  RST,
  input  [3:0] MANUAL,
  input  [3:0] ADDRESS,
  input  in_14,
  input  [1:0] in_15,
  input  GPR_LD,
  input  INC,
  output [3:0] DRAM_output,
  output [3:0] IR,
  output [3:0] GPR_Input
);

  wire [3:0] gpr_1_stored_value, multiplexer_1_out, pc_1_pc_plus_1;

  PC pc_1 (.INC(INC), .Manual_Address(ADDRESS), .CLK(CLK), .RST(RST), .LD(IR_LD), .PC_plus_1(pc_1_pc_plus_1));
  Multiplexer #(.Bits(4)) multiplexer_1 (
    .sel(in_14), .in_0(pc_1_pc_plus_1), .in_1(gpr_1_stored_value), .out(multiplexer_1_out));
  RAMSinglePortSel #(.AddrBits(4), .Bits(4)) ramsingleportsel (
    .A(multiplexer_1_out), .CS(nCS), .WE(nOE), .OE(nRW), .D(Data));
  GPR gpr_1 (
    .CLK(CLK), .LD(GPR_LD), .ST(1'b1), .D(GPR_Input), .CLR(RST), .Sel_Reg(in_15), .Sel_Register(in_15),
    .Stored_Value(gpr_1_stored_value));  // open: READ
  assign DRAM_output = IR_LD ? Data : 4'bz;  // Driver driver_1
  assign GPR_Input = GPR_LD ? Data : 4'bz;  // Driver driver_2
  IR ir_1 (.CLK(CLK), .RST(RST), .Manual(MANUAL), .DRAM_output(DRAM_output), .LD(IR_LD), .sel(SEL), .IR_out(IR));

  // Notes on the sheet:
  //   nOE: default 1
  //   nRW: default 1
  //   nCS: default 1
  //   Tri-State Buffer
endmodule
